# Fritzing sketch Alarma (saved by Fritzing 0.9.3b)
breadboards: 1

parts:
  S1 = SWITCH-MOMENTARY-2 [package=reed_switch_plastic]
  J1 = Piezo Speaker
  LED1 = LED - 5mm [color="Red (633nm)" package="5 mm [THT]"]
  R1 = Resistor [tolerance=±5% resistance=220 package=THT]
  R2 = Resistor [tolerance=±5% resistance=10k package=THT]
  R3 = Resistor [tolerance=±5% resistance=220 package=THT]
  Componente1 = Arduino Ethernet Shield (Rev3)

nets:
  N1: S1.1, Componente1.5V
  N2: S1.2, R2.Pin_0
  N3: J1.pin1, LED1.cathode, R2.Pin_1, Componente1.D2, Componente1.GND
  N4: J1.pin2, R3.Pin_0
  N5: LED1.anode, R1.Pin_0
  N6: R1.Pin_1, Componente1.ETH_CS
  N7: R3.Pin_1, Componente1.D8
